// Logisim project alu.circ as structural Verilog: 9 circuits, main circuit alu
module alu (
  input  [31:0] A,
  input  [31:0] B,
  input  [3:0] ALUSel,
  output [31:0] Result
);

  wire [31:0] add0, and1, divu8, mul10, mulh14, mulhu11, or2, remu9, sll6, slt7, sra5, srl4, sub12, xor3;

  srl32 srl32_1 (.in_1(A), .in_2(B), .out_3(srl4));
  sra32 sra32_1 (.in_1(A), .in_2(B), .out_3(sra5));
  sll32 sll32_1 (.in_1(A), .in_2(B), .out_3(sll6));
  slt32 slt32_1 (.in_1(A), .in_2(B), .out_3(slt7));
  Subtractor #(.width(32)) subtractor_1 (.a(A), .b(B), .out(sub12));  // open: bin, bout
  remu32 remu32_1 (.in_1(A), .in_2(B), .out_3(remu9));
  mulh32 mulh32_1 (.in_1(A), .in_2(B), .out_3(mulh14));
  assign or2 = A | B;  // OR_Gate or_1, 32 bits wide
  Adder #(.width(32)) adder_1 (.a(A), .b(B), .out(add0));  // open: cin, cout
  assign and1 = A & B;  // AND_Gate and_1, 32 bits wide
  assign xor3 = A ^ B;  // XOR_Gate xor_1, 32 bits wide
  Divider #(.width(32)) divider_1 (.a(A), .b(B), .out(divu8));  // open: upper, rem
  mul32 mul32_1 (.in_1(A), .in_2(B), .out_3(mul10), .out_4(mulhu11));
  Multiplexer #(.select(4), .width(32), .enable("false")) multiplexer_1 (
    .in0(add0), .in1(and1), .in2(or2), .in3(xor3), .in4(srl4), .in5(sra5), .in6(sll6), .in7(slt7),
    .in8(divu8), .in9(remu9), .in10(mul10), .in11(mulhu11), .in12(sub12), .in13(B), .in14(mulh14),
    .out(Result), .sel(ALUSel));  // open: in15

  // Other names for the same wires on the sheet: bsel13[31:0] = B

  // Notes on the sheet:
  //   INPUTS to your circuit
  //   DON'T CHANGE THE LOCATIONS OF THE INPUTS AND OUTPUTS!
  //   OUTPUT from your circuit
endmodule

module srl32 (
  input  [31:0] in_1,
  input  [31:0] in_2,
  output [31:0] out_3
);

  Shifter #(.width(32), .shift("lr")) shifter_1 (.in(in_1), .\dist (in_2[4:0]), .out(out_3));
endmodule

module sra32 (
  input  [31:0] in_1,
  input  [31:0] in_2,
  output [31:0] out_3
);

  Shifter #(.width(32), .shift("ar")) shifter_1 (.in(in_1), .\dist (in_2[4:0]), .out(out_3));
endmodule

module sll32 (
  input  [31:0] in_1,
  input  [31:0] in_2,
  output [31:0] out_3
);

  Shifter #(.width(32)) shifter_1 (.in(in_1), .\dist (in_2[4:0]), .out(out_3));
endmodule

module remu32 (
  input  [31:0] in_1,
  input  [31:0] in_2,
  output [31:0] out_3
);

  wire [31:0] bm, divider_1_out;

  Divider #(.width(32)) divider_1 (.a(in_1), .b(in_2), .out(divider_1_out));  // open: upper, rem
  Subtractor #(.width(32)) subtractor_1 (.a(in_1), .b(bm), .out(out_3));  // open: bin, bout
  Multiplier #(.width(32)) multiplier_1 (.a(divider_1_out), .b(in_2), .out(bm));  // open: cin, cout
endmodule

module mul32 (
  input  [31:0] in_1,
  input  [31:0] in_2,
  output [31:0] out_3,
  output [31:0] out_4
);

  Multiplier #(.width(32)) multiplier_1 (.a(in_1), .b(in_2), .out(out_3), .cout(out_4));  // open: cin
endmodule

module mulh32 (
  input  [31:0] in_1,
  input  [31:0] in_2,
  output [31:0] out_3
);

  wire xor_1_out;
  wire [31:0] multiplexer_1_out, multiplexer_2_out, multiplier_1_cout, multiplier_1_out, negator_1_out,
       negator_2_out, usemulh_1_out_3;

  Negator #(.width(32)) negator_1 (.in(in_2), .out(negator_1_out));
  Negator #(.width(32)) negator_2 (.in(in_1), .out(negator_2_out));
  Multiplexer #(.width(32), .enable("false")) multiplexer_1 (
    .in0(in_1), .in1(negator_2_out), .out(multiplexer_1_out), .sel(in_1[31]));
  Multiplexer #(.width(32), .enable("false")) multiplexer_2 (
    .in0(in_2), .in1(negator_1_out), .out(multiplexer_2_out), .sel(in_2[31]));
  Multiplier #(.width(32)) multiplier_1 (
    .a(multiplexer_1_out), .b(multiplexer_2_out), .out(multiplier_1_out), .cout(multiplier_1_cout));  // open: cin
  Multiplexer #(.width(32), .enable("false")) multiplexer_3 (
    .in0(multiplier_1_cout), .in1(usemulh_1_out_3), .out(out_3), .sel(xor_1_out));
  xor xor_1 (xor_1_out, in_1[31], in_2[31]);
  usemulh usemulh_1 (.in_1(multiplier_1_cout), .in_2(multiplier_1_out), .out_3(usemulh_1_out_3));

  // Other names for the same wires on the sheet: AN = in_1[31]; BN = in_2[31]
endmodule

module slt32 (
  input  [31:0] in_1,
  input  [31:0] in_2,
  output [31:0] out_3
);

  Comparator #(.width(32)) comparator_1 (.a(in_1), .b(in_2), .lt(out_3[0]));  // open: gt, eq

  assign out_3[31:1] = {31{1'b0}};
endmodule

module usemulh (
  input  [31:0] in_1,
  input  [31:0] in_2,
  output [31:0] out_3
);

  wire comparator_1_eq;
  wire [0:0] not_1_out;
  wire [31:0] negator_1_out;

  Negator #(.width(32)) negator_1 (.in(in_1), .out(negator_1_out));
  Comparator #(.width(32)) comparator_1 (.a(in_2), .b({32{1'b0}}), .eq(comparator_1_eq));  // open: gt, lt
  not not_1 (not_1_out[0], comparator_1_eq);
  Subtractor #(.width(32)) subtractor_1 (
    .a(negator_1_out), .b({{31{1'b0}}, not_1_out[0]}), .out(out_3));  // open: bin, bout
endmodule
