// Logisim project branch_comp.circ as structural Verilog: 1 circuit, main circuit branch_comp
module branch_comp (
  input  [31:0] rs1,
  input  [31:0] rs2,
  input  BrUn,
  output BrEq,
  output BrLt
);

  wire BrEq1, BrEq2, BrLt1, BrLt2;

  Comparator #(.width(32)) comparator_1 (.a(rs1), .b(rs2), .eq(BrEq1), .lt(BrLt1));  // open: gt
  Comparator #(.width(32), .mode("unsigned")) comparator_2 (.a(rs1), .b(rs2), .eq(BrEq2), .lt(BrLt2));  // open: gt
  Multiplexer #(.enable("false")) multiplexer_1 (.in0(BrEq1), .in1(BrEq2), .out(BrEq), .sel(BrUn));
  Multiplexer #(.enable("false")) multiplexer_2 (.in0(BrLt1), .in1(BrLt2), .out(BrLt), .sel(BrUn));

  // Notes on the sheet:
  //   INPUTS to your circuit
  //   DON'T CHANGE THE LOCATIONS OF THE INPUTS AND OUTPUTS!
  //   OUTPUT from your circuit
endmodule
