// Logisim project control_logic.circ as structural Verilog: 1 circuit, main circuit control_logic
module control_logic (
  input  [31:0] inst,
  input  BrEq,
  input  BrLt,
  output PCSel,
  output RegWEn,
  output [2:0] ImmSel,
  output BrUn,
  output ASel,
  output BSel,
  output [3:0] ALUSel,
  output MemRW,
  output [1:0] WBSel
);

  wire and_1_out, and_2_out, and_4_out, and_5_out, and_8_out, and_9_out, and_12_out, and_13_out, BrGt, isbeq,
       isbge, isbgeu, isblt, isbltu, isbne, isI13, isJAL, isJALR, isR, isSB, isSR5, isSR20, isU, isU1, isU2,
       JustJump, not_1_out, not_2_out, not_3_out, not_4_out, not_5_out, or_2_out, or_4_out, or_5_out,
       or_6_out, or_7_out, PCFirst, PCSel1, PCSel2, PCSel3, PCSel4, PCSel5, PCSel6;
  wire [6:0] SRconst;
  wire [9:0] infunct;
  wire [15:15] rom_1_data;

  and and_1 (and_1_out, isI13, isSR5);
  Multiplexer #(.width(7), .enable("false")) multiplexer_1 (
    .in0({7{1'b0}}), .in1(7'b0100000), .out(SRconst), .sel(and_2_out));
  and and_2 (and_2_out, and_1_out, isSR20);
  not not_1 (not_1_out, BrEq);
  not not_2 (not_2_out, BrLt);
  Multiplexer #(.width(7), .enable("false")) multiplexer_2 (
    .in0(SRconst), .in1(inst[31:25]), .out(infunct[6:0]), .sel(isR));
  and and_3 (BrGt, not_1_out, not_2_out);
  Comparator #(.width(7)) comparator_1 (.a(inst[6:0]), .b(7'b1100011), .eq(isSB));  // open: gt, lt
  Comparator #(.width(7)) comparator_2 (.a(inst[6:0]), .b(7'b0110011), .eq(isR));  // open: gt, lt
  not not_3 (not_3_out, BrLt);
  ROM #(.addrWidth(17), .dataWidth(16)) rom_1 (
    .addr({inst[6:0], infunct}),
    .data({rom_1_data[15], PCFirst, RegWEn, ImmSel, BrUn, ASel, BSel, ALUSel, MemRW, WBSel}));
  and and_4 (and_4_out, isbltu, BrLt);
  and and_5 (and_5_out, isbge, not_3_out);
  and and_6 (PCSel5, PCFirst, and_4_out);
  and and_7 (PCSel6, PCFirst, and_5_out);
  Comparator #(.width(7)) comparator_3 (.a(inst[6:0]), .b(7'b0010011), .eq(isI13));  // open: gt, lt
  Comparator #(.width(7)) comparator_4 (.a(inst[31:25]), .b(7'b0100000), .eq(isSR20));  // open: gt, lt
  Comparator #(.width(3)) comparator_5 (.a(inst[14:12]), .b(3'b101), .eq(isSR5));  // open: gt, lt
  // Probe on {rom_1_data[15], PCFirst, RegWEn, ImmSel, BrUn, ASel, BSel, ALUSel, MemRW, WBSel}
  not not_4 (not_4_out, BrLt);
  // Probe on infunct[9:7]
  and and_8 (and_8_out, isblt, BrLt);
  and and_9 (and_9_out, isbge, not_4_out);
  and and_10 (PCSel3, PCFirst, and_8_out);
  and and_11 (PCSel4, PCFirst, and_9_out);
  // Probe on infunct[6:0]
  // Probe on inst[6:0]
  // Probe on {inst[6:0], infunct}
  not not_5 (not_5_out, BrEq);
  Comparator #(.width(3)) comparator_6 (.a(inst[14:12]), .b(3'b000), .eq(isbeq));  // open: gt, lt
  Comparator #(.width(3)) comparator_7 (.a(inst[14:12]), .b(3'b001), .eq(isbne));  // open: gt, lt
  Comparator #(.width(3)) comparator_8 (.a(inst[14:12]), .b(3'b100), .eq(isblt));  // open: gt, lt
  Comparator #(.width(3)) comparator_9 (.a(inst[14:12]), .b(3'b101), .eq(isbge));  // open: gt, lt
  Comparator #(.width(3)) comparator_10 (.a(inst[14:12]), .b(3'b110), .eq(isbltu));  // open: gt, lt
  Comparator #(.width(3)) comparator_11 (.a(inst[14:12]), .b(3'b111), .eq(isbgeu));  // open: gt, lt
  and and_12 (and_12_out, isbeq, BrEq);
  and and_13 (and_13_out, isbne, not_5_out);
  and and_14 (PCSel1, PCFirst, and_12_out);
  and and_15 (PCSel2, PCFirst, and_13_out);
  Comparator #(.width(7)) comparator_12 (.a(inst[6:0]), .b(7'b0110111), .eq(isU2));  // open: gt, lt
  or or_1 (isU, isU1, isU2);
  Multiplexer #(.width(3), .enable("false")) multiplexer_3 (
    .in0(inst[14:12]), .in1(3'b000), .out(infunct[9:7]), .sel(isU));
  Comparator #(.width(7)) comparator_13 (.a(inst[6:0]), .b(7'b0010111), .eq(isU1));  // open: gt, lt
  or or_2 (or_2_out, JustJump, PCSel6);
  Comparator #(.width(7)) comparator_14 (.a(inst[6:0]), .b(7'b1101111), .eq(isJAL));  // open: gt, lt
  Comparator #(.width(7)) comparator_15 (.a(inst[6:0]), .b(7'b1100111), .eq(isJALR));  // open: gt, lt
  or or_3 (JustJump, isJAL, isJALR);
  or or_4 (or_4_out, PCSel5, or_2_out);
  or or_5 (or_5_out, PCSel3, or_6_out);
  or or_6 (or_6_out, PCSel4, or_4_out);
  or or_7 (or_7_out, PCSel2, or_5_out);
  or or_8 (PCSel, PCSel1, or_7_out);

  // Other names for the same wires on the sheet: usefunct7[6:0] = infunct[6:0]; usefunct3[2:0] = infunct[9:7];
  //   infunct[16:10] = inst[6:0]; opcode[6:0] = inst[6:0]; funct3[2:0] = inst[14:12]; funct7[6:0] = inst[31:25]

  // Notes on the sheet:
  //   INPUTS to your circuit
  //   contents of rom_1 (hex, n*v repeats v):
  //   1111 2222 3333 4444 5555 6666 3066*0 2080 127*0 2080 127*0 2080 16127*0 2081 127*0 20b1 127*0 20b9
  //   255*0 2099 127*0 20a1 31*0 20a9 95*0 2091 127*0 2089 3199*0 2d81 12543*0 484 16127*0 2001 2051 30*0
  //   2061 95*0 2031 2071 126*0 2039 128*0 2059 126*0 2019 127*0 2021 2041 30*0 2029 95*0 2011 127*0 2001
  //   2049 3198*0 2ce9 45055*0 4980 127*0 4980 383*0 4980 127*0 4980 127*0 4b80 127*0 4b80 3199*0 6082
  //   8191*0 7182
  //   DON'T CHANGE THE LOCATIONS OF THE INPUTS AND OUTPUTS!
  //   OUTPUT from your circuit
endmodule
