// Logisim project cpu.circ as structural Verilog: 2 circuits, main circuit main
module main (
  input  [31:0] INSTRUCTION,
  input  CLOCK,
  output [31:0] PROGRAM_COUNTER,
  output [31:0] ra,
  output [31:0] sp,
  output [31:0] t0,
  output [31:0] t1,
  output [31:0] t2,
  output [31:0] s0,
  output [31:0] s1,
  output [31:0] a0
);

  wire ASel, BrEq, BrLt, BrUn, BSel, control_logic_1_memrw, PCSel, RegWEn;
  wire [1:0] control_logic_1_wbsel;
  wire [2:0] control_logic_1_immsel;
  wire [3:0] control_logic_1_alusel;
  wire [4:0] rdUse, rs1Use, rs2Use;
  wire [31:0] adder_1_out, adder_2_out, ALUout, DMEM_p5, immOut, INSTRUCTION_USE, multiplexer_1_out,
       multiplexer_2_out, multiplexer_3_out, multiplexer_4_out, PC_USE, rs1Out, rs2Out, wbUse;

  control_logic control_logic_1 (
    .BSel(BSel), .ASel(ASel), .BrUn(BrUn), .ImmSel(control_logic_1_immsel), .RegWEn(RegWEn), .PCSel(PCSel),
    .BrLt(BrLt), .BrEq(BrEq), .inst(INSTRUCTION_USE), .ALUSel(control_logic_1_alusel),
    .MemRW(control_logic_1_memrw), .WBSel(control_logic_1_wbsel));
  Adder #(.width(32)) adder_1 (.a(PROGRAM_COUNTER), .b(32'h4), .out(adder_1_out));  // open: cin, cout
  Multiplexer #(.width(32), .enable("false")) multiplexer_1 (
    .in0(INSTRUCTION), .in1(32'h13), .out(multiplexer_1_out), .sel(PCSel));
  Multiplexer #(.width(32), .enable("false")) multiplexer_2 (
    .in0(adder_1_out), .in1(ALUout), .out(multiplexer_2_out), .sel(PCSel));
  Register #(.width(32)) PC (.D(multiplexer_2_out), .clk(CLOCK), .Q(PROGRAM_COUNTER));  // open: en, clr
  imm_gen imm_gen_1 (.ImmSel(control_logic_1_immsel), .inst(INSTRUCTION_USE), .imm(immOut));
  Register #(.width(32)) register_1 (.D(multiplexer_1_out), .en(1'b1), .clk(CLOCK), .Q(INSTRUCTION_USE));  // open: clr
  Register #(.width(32)) register_2 (.D(PROGRAM_COUNTER), .en(1'b1), .clk(CLOCK), .Q(PC_USE));  // open: clr
  // Probe on INSTRUCTION_USE
  // Probe on PC_USE
  branch_comp branch_comp_1 (.BrEq(BrEq), .BrUn(BrUn), .rs1(rs1Out), .BrLt(BrLt), .rs2(rs2Out));
  regfile_main RegFile (
    .rs2(rs2Use), .rd(rdUse), .Read_Data_1(rs1Out), .Read_Data_2(rs2Out), .ra(ra), .sp(sp), .t0(t0), .t1(t1),
    .t2(t2), .s0(s0), .s1(s1), .a0(a0), .rs1(rs1Use), .Write_Data(wbUse), .RegWEn(RegWEn), .clk(CLOCK));
  InsParse insparse_1 (.in_1(INSTRUCTION_USE), .rd(rdUse), .rs1(rs1Use), .rs2(rs2Use));  // open: opcode, funct3, funct7
  Multiplexer #(.width(32), .enable("false")) multiplexer_3 (
    .in0(rs1Out), .in1(PC_USE), .out(multiplexer_3_out), .sel(ASel));
  Multiplexer #(.width(32), .enable("false")) multiplexer_4 (
    .in0(rs2Out), .in1(immOut), .out(multiplexer_4_out), .sel(BSel));
  alu Arithmetic_Logic_Unit (
    .Result(ALUout), .ALUSel(control_logic_1_alusel), .A(multiplexer_3_out), .B(multiplexer_4_out));
  Adder #(.width(32)) adder_2 (.a(PC_USE), .b(32'h4), .out(adder_2_out));  // open: cin, cout
  // mem_main DMEM: pin names not known; wires that end beside it: ALUout, rs2Out, CLOCK, control_logic_1_memrw, DMEM_p5
  Multiplexer #(.select(2), .width(32), .enable("false")) multiplexer_5 (
    .in0(DMEM_p5), .in1(ALUout), .in2(adder_2_out), .out(wbUse), .sel(control_logic_1_wbsel));  // open: in3

  // Other names for the same wires on the sheet: clk = CLOCK

  // Notes on the sheet:
  //   Output
  //   IMEM (do **NOT** move this)
  //   Inputs
  //   It is OK to move the PC, RegFile, ALU, MEM, Branch Comp, Imm Gen, and Control Logic to wherever is most convenient for you when constructing your CPU, and to delete this text
  //   Inputs/Outputs for testing. Do **NOT** move these.
endmodule

module InsParse (
  input  [31:0] in_1,
  output [6:0] opcode,
  output [4:0] rd,
  output [2:0] funct3,
  output [4:0] rs1,
  output [4:0] rs2,
  output [6:0] funct7
);


  assign funct3 = in_1[14:12];
  assign funct7 = in_1[31:25];
  assign opcode = in_1[6:0];
  assign rd = in_1[11:7];
  assign rs1 = in_1[19:15];
  assign rs2 = in_1[24:20];
endmodule
