// Logisim project regfile.circ as structural Verilog
module main (
  input  [4:0] rs1,
  input  [4:0] rs2,
  input  [4:0] rd,
  input  [31:0] Write_Data,
  input  RegWEn,
  input  clk,
  output [31:0] ra,
  output [31:0] sp,
  output [31:0] t0,
  output [31:0] t1,
  output [31:0] t2,
  output [31:0] s0,
  output [31:0] s1,
  output [31:0] a0,
  output [31:0] Read_Data_1,
  output [31:0] Read_Data_2
);

  wire a0w, and_1_out, raw, s0w, s1w, spw, t0w, t1w, t2w;

  Register #(.width(32)) register_1 (.D(Write_Data), .en(raw), .clk(clk), .Q(ra));  // open: clr
  Register #(.width(32)) register_2 (.D(Write_Data), .en(t2w), .clk(clk), .Q(t2));  // open: clr
  Register #(.width(32)) register_3 (.D(Write_Data), .en(spw), .clk(clk), .Q(sp));  // open: clr
  Register #(.width(32)) register_4 (.D(Write_Data), .en(s0w), .clk(clk), .Q(s0));  // open: clr
  Register #(.width(32)) register_5 (.D(Write_Data), .en(t0w), .clk(clk), .Q(t0));  // open: clr
  Register #(.width(32)) register_6 (.D(Write_Data), .en(s1w), .clk(clk), .Q(s1));  // open: clr
  Register #(.width(32)) register_7 (.D(Write_Data), .en(t1w), .clk(clk), .Q(t1));  // open: clr
  Register #(.width(32)) register_8 (.D(Write_Data), .en(a0w), .clk(clk), .Q(a0));  // open: clr
  and and_1 (and_1_out, RegWEn, 1'b1);
  Demultiplexer #(.select(5), .enable("false")) demultiplexer_1 (
    .out1(raw), .out2(spw), .out5(t0w), .out6(t1w), .out7(t2w), .out8(s0w), .out9(s1w), .out10(a0w),
    .in(and_1_out), .sel(rd));  // open: out0, out3, out4, out11, out12, out13, out14, out15, out16, out17, out18, out19, out20, out21, out22, out23, out24, out25, out26, out27, out28, out29, out30, out31
  Multiplexer #(.select(5), .width(32), .enable("false")) multiplexer_1 (
    .in0({32{1'b0}}), .in1(ra), .in2(sp), .in3(sp), .in4(sp), .in5(t0), .in6(t1), .in7(t2), .in8(s0),
    .in9(s1), .in10(a0), .in11(a0), .in12(a0), .in13(a0), .in14(a0), .in15(a0), .in16(a0), .in17(a0),
    .in18(a0), .in19(a0), .in20(a0), .in21(a0), .in22(a0), .in23(a0), .in24(a0), .in25(a0), .in26(a0),
    .in27(a0), .in28(a0), .in29(a0), .in30(a0), .in31(a0), .out(Read_Data_1), .sel(rs1));
  Multiplexer #(.select(5), .width(32), .enable("false")) multiplexer_2 (
    .in0({32{1'b0}}), .in1(ra), .in2(sp), .in3(sp), .in4(sp), .in5(t0), .in6(t1), .in7(t2), .in8(s0),
    .in9(s1), .in10(a0), .in11(a0), .in12(a0), .in13(a0), .in14(a0), .in15(a0), .in16(a0), .in17(a0),
    .in18(a0), .in19(a0), .in20(a0), .in21(a0), .in22(a0), .in23(a0), .in24(a0), .in25(a0), .in26(a0),
    .in27(a0), .in28(a0), .in29(a0), .in30(a0), .in31(a0), .out(Read_Data_2), .sel(rs2));

  // Other names for the same wires on the sheet: read_data1[31:0] = Read_Data_1; read_data2[31:0] = Read_Data_2;
  //   read_reg1[4:0] = rs1; read_reg2[4:0] = rs2; write_en = RegWEn; write_reg[4:0] = rd

  // Notes on the sheet:
  //   INPUTS to your circuit
  //   DON'T CHANGE THE LOCATIONS OF THE INPUTS AND OUTPUTS!
  //   These are DEBUG/TEST outputs from your circuit.
  //   OUTPUTS from your circuit
endmodule
